// Logisim project computer-architecture-project.circ as structural Verilog: 7 circuits, main circuit Program_Counter
module Main_Microprocessor (
  input  in_1,
  input  in_2
);

  wire alu_1_equal, clock_1_out, control_unit_1_out_2, control_unit_1_out_3, control_unit_1_out_4,
       control_unit_1_out_5, control_unit_1_out_6, control_unit_1_out_7, control_unit_1_out_8,
       multiplexer_2_out, multiplexer_5_out, not_1_out;
  wire [2:0] alu_control_unit_1_out_2, multiplexer_6_out;
  wire [7:0] adder_1_out, bit_extender_1_out, bit_extender_3_out, bit_extender_4_out, multiplexer_1_out,
       multiplexer_3_out, multiplexer_4_out, program_counter_1_out_4, register_1_q_2;
  wire [15:0] alu_1_out_4, bit_extender_2_out, multiplexer_7_out, multiplexer_8_out, ram_2_data,
       register_file_1_out_7, register_file_1_out_8;
  wire [23:0] ram_1_data, register_1_q;

  Multiplexer #(.width(8), .enable("false")) multiplexer_1 (
    .in0(multiplexer_3_out), .in1(register_1_q_2), .out(multiplexer_1_out), .sel(control_unit_1_out_8));
  Adder adder_1 (.a(8'h1), .b(program_counter_1_out_4), .out(adder_1_out));  // open: cin, cout
  Program_Counter program_counter_1 (
    .in_1(multiplexer_1_out), .out_4(program_counter_1_out_4), .in_2(clock_1_out), .in_3(in_2));
  Clock clock_1 (.out(clock_1_out));
  Multiplexer #(.enable("false")) multiplexer_2 (
    .in0(1'b0), .in1(multiplexer_5_out), .out(multiplexer_2_out), .sel(control_unit_1_out_6));
  Multiplexer #(.width(8), .enable("false")) multiplexer_3 (
    .in0(multiplexer_4_out), .in1(bit_extender_1_out), .out(multiplexer_3_out), .sel(control_unit_1_out_7));
  Multiplexer #(.width(8), .enable("false")) multiplexer_4 (
    .in0(adder_1_out), .in1(bit_extender_3_out), .out(multiplexer_4_out), .sel(multiplexer_2_out));
  Multiplexer #(.enable("false")) multiplexer_5 (
    .in0(not_1_out), .in1(alu_1_equal), .out(multiplexer_5_out), .sel(control_unit_1_out_5));
  Bit_Extender #(.in_width(13), .out_width(8)) bit_extender_1 (
    .in({register_1_q_2, register_1_q[4:0]}), .out(bit_extender_1_out));
  RAM #(.dataWidth(24)) ram_1 (
    .addr(program_counter_1_out_4), .data(ram_1_data), .clk(clock_1_out));  // open: sel, ld, clr
  not not_1 (not_1_out, alu_1_equal);
  Register #(.width(24)) register_1 (
    .D(ram_1_data), .Q({register_1_q[23:13], register_1_q_2, register_1_q[4:0]}), .clk(clock_1_out),
    .clr(in_2));  // open: en
  assign bit_extender_2_out = {{3{register_1_q_2[7]}}, {register_1_q_2, register_1_q[4:0]}};  // Bit_Extender bit_extender_2
  Bit_Extender #(.in_width(16), .out_width(8)) bit_extender_3 (.in(register_file_1_out_7), .out(bit_extender_3_out));
  Multiplexer #(.width(3), .enable("false")) multiplexer_6 (
    .in0(register_1_q_2[7:5]), .in1(register_1_q[18:16]), .out(multiplexer_6_out), .sel(control_unit_1_out_2));
  Control_Unit control_unit_1 (
    .in_1(register_1_q[23:19]), .out_2(control_unit_1_out_2), .out_3(control_unit_1_out_3),
    .out_4(control_unit_1_out_4), .out_5(control_unit_1_out_5), .out_6(control_unit_1_out_6),
    .out_7(control_unit_1_out_7), .out_8(control_unit_1_out_8));
  Register_File register_file_1 (
    .in_1(register_1_q[15:13]), .in_2(multiplexer_6_out), .in_3(register_1_q[18:16]),
    .in_4(multiplexer_8_out), .in_5(clock_1_out), .out_7(register_file_1_out_7),
    .out_8(register_file_1_out_8), .in_6(in_2));
  Multiplexer #(.width(16), .enable("false")) multiplexer_7 (
    .in0(register_file_1_out_8), .in1(bit_extender_2_out), .out(multiplexer_7_out), .sel(control_unit_1_out_4));
  ALU_Control_Unit alu_control_unit_1 (.in_1(register_1_q[23:19]), .out_2(alu_control_unit_1_out_2));
  ALU alu_1 (
    .in_2(register_file_1_out_7), .in_3(multiplexer_7_out), .out_4(alu_1_out_4), .Equal(alu_1_equal),
    .in_1(alu_control_unit_1_out_2));  // open: Zero, Carry, Overflow, Is_less_than
  Multiplexer #(.width(16), .enable("false")) multiplexer_8 (
    .in0(alu_1_out_4), .in1(ram_2_data), .out(multiplexer_8_out), .sel(control_unit_1_out_3));
  Bit_Extender #(.in_width(16), .out_width(8)) bit_extender_4 (.in(alu_1_out_4), .out(bit_extender_4_out));
  RAM #(.dataWidth(16), .bus("separate")) ram_2 (
    .addr(bit_extender_4_out), .din(register_file_1_out_8), .data(ram_2_data), .str(control_unit_1_out_2),
    .clk(clock_1_out), .clr(in_1));  // open: sel, ld

  // Notes on the sheet:
  //   - Single cycle -
  //   The MIPS 16-bit Microprocessor
  //   Designed by; Bari BGF
  //   On: July 29th, 2023
endmodule

module Program_Counter (
  input  [7:0] in_1,
  input  in_2,
  input  in_3,
  output [7:0] out_4
);

  Register register_1 (.D(in_1), .Q(out_4), .clk(in_2), .clr(in_3));  // open: en
endmodule

module Register_File (
  input  [2:0] in_1,
  input  [2:0] in_2,
  input  [2:0] in_3,
  input  [15:0] in_4,
  input  in_5,
  input  in_6,
  output [15:0] out_7,
  output [15:0] out_8
);

  wire demultiplexer_2_out1, demultiplexer_2_out2, demultiplexer_2_out3, demultiplexer_2_out4,
       demultiplexer_2_out5;
  wire [15:0] demultiplexer_1_out1, demultiplexer_1_out2, demultiplexer_1_out3, demultiplexer_1_out4,
       demultiplexer_1_out5, register_1_q, register_2_q, register_3_q, register_4_q, register_5_q;

  Demultiplexer #(.select(3), .width(16), .enable("false")) demultiplexer_1 (
    .out1(demultiplexer_1_out1), .out2(demultiplexer_1_out2), .out3(demultiplexer_1_out3),
    .out4(demultiplexer_1_out4), .out5(demultiplexer_1_out5), .in(in_4), .sel(in_3));  // open: out0, out6, out7
  Demultiplexer #(.select(3), .enable("false")) demultiplexer_2 (
    .out1(demultiplexer_2_out1), .out2(demultiplexer_2_out2), .out3(demultiplexer_2_out3),
    .out4(demultiplexer_2_out4), .out5(demultiplexer_2_out5), .in(1'b1), .sel(in_3));  // open: out0, out6, out7
  Register #(.width(16)) register_1 (
    .D(demultiplexer_1_out1), .en(demultiplexer_2_out1), .Q(register_1_q), .clk(in_5), .clr(in_6));
  Register #(.width(16)) register_2 (
    .D(demultiplexer_1_out2), .en(demultiplexer_2_out2), .Q(register_2_q), .clk(in_5), .clr(in_6));
  Register #(.width(16)) register_3 (
    .D(demultiplexer_1_out3), .en(demultiplexer_2_out3), .Q(register_3_q), .clk(in_5), .clr(in_6));
  Register #(.width(16)) register_4 (
    .D(demultiplexer_1_out4), .en(demultiplexer_2_out4), .Q(register_4_q), .clk(in_5), .clr(in_6));
  Register #(.width(16)) register_5 (
    .D(demultiplexer_1_out5), .en(demultiplexer_2_out5), .Q(register_5_q), .clk(in_5), .clr(in_6));
  Multiplexer #(.select(3), .width(16), .enable("false")) multiplexer_1 (
    .in1(register_1_q), .in2(register_2_q), .in3(register_3_q), .in4(register_4_q), .in5(register_5_q),
    .out(out_7), .sel(in_1));  // open: in0, in6, in7
  Multiplexer #(.select(3), .width(16), .enable("false")) multiplexer_2 (
    .in1(register_1_q), .in2(register_2_q), .in3(register_3_q), .in4(register_4_q), .in5(register_5_q),
    .out(out_8), .sel(in_2));  // open: in0, in6, in7

  // Notes on the sheet:
  //   rs
  //   rt
  //   rd
  //   lo
  //   hi
endmodule

module ALU (
  input  [2:0] in_1,
  input  [15:0] in_2,
  input  [15:0] in_3,
  output [15:0] out_4,
  output Zero,
  output Carry,
  output Overflow,
  output Equal,
  output Is_less_than
);

  wire adder_1_cout, and_2_out, and_3_out, and_4_out, and_5_out, and_6_out, and_7_out, bitfinder_1_found,
       bitfinder_2_found, bitfinder_3_found, bitselector_1_out, bitselector_2_out, bitselector_3_out,
       bitselector_4_out, comparator_3_eq, subtractor_1_bout, xnor_1_out, xor_2_out;
  wire [1:0] bit_extender_1_out;
  wire [15:0] adder_1_out, and_1_out, multiplier_1_cout, multiplier_1_out, or_1_out, subtractor_1_out,
       xor_1_out;

  Adder #(.width(16)) adder_1 (.a(in_2), .b(in_3), .out(adder_1_out), .cout(adder_1_cout));  // open: cin
  Subtractor #(.width(16)) subtractor_1 (
    .a(in_2), .b(in_3), .out(subtractor_1_out), .bout(subtractor_1_bout));  // open: bin
  Multiplier #(.width(16)) multiplier_1 (
    .a(in_2), .b(in_3), .out(multiplier_1_out), .cout(multiplier_1_cout));  // open: cin
  assign and_1_out = in_2 & in_3;  // AND_Gate and_1, 16 bits wide
  assign or_1_out = in_2 | in_3;  // OR_Gate or_1, 16 bits wide
  assign xor_1_out = in_2 ^ in_3;  // XOR_Gate xor_1, 16 bits wide
  Comparator #(.width(16)) comparator_1 (.a(in_2), .b(in_3), .eq(Equal), .lt(Is_less_than));  // open: gt
  Multiplexer #(.select(3), .width(16), .enable("false")) multiplexer_1 (
    .in1(adder_1_out), .in2(subtractor_1_out), .in3(multiplier_1_out), .in4(and_1_out), .in5(or_1_out),
    .in6(xor_1_out), .out(out_4), .sel(in_1));  // open: in0, in7
  Bit_Extender #(.in_width(3), .out_width(2)) bit_extender_1 (.in(in_1), .out(bit_extender_1_out));
  BitFinder #(.width(16)) bitfinder_1 (.in(multiplier_1_cout), .found(bitfinder_1_found));  // open: index
  BitSelector #(.width(16)) bitselector_1 (.in(in_2), .out(bitselector_1_out), .sel(4'b1111));
  BitSelector #(.width(16)) bitselector_2 (.in(in_3), .out(bitselector_2_out), .sel(4'b1111));
  Comparator #(.width(16)) comparator_2 (.a(out_4), .b({16{1'b0}}), .eq(Zero));  // open: gt, lt
  Multiplexer #(.select(2), .enable("false")) multiplexer_2 (
    .in1(adder_1_cout), .in2(subtractor_1_bout), .in3(bitfinder_1_found), .out(Carry),
    .sel(bit_extender_1_out));  // open: in0
  BitSelector #(.width(16)) bitselector_3 (.in(out_4), .out(bitselector_3_out), .sel(4'b1111));
  xnor xnor_1 (xnor_1_out, bitselector_1_out, bitselector_2_out);
  and and_2 (and_2_out, ~bitselector_2_out, bitselector_1_out);  // AND_Gate
  BitFinder #(.width(16)) bitfinder_2 (.in(in_2), .found(bitfinder_2_found));  // open: index
  and and_3 (and_3_out, bitfinder_2_found, bitfinder_3_found);
  BitFinder #(.width(16)) bitfinder_3 (.in(in_3), .found(bitfinder_3_found));  // open: index
  xor xor_2 (xor_2_out, bitselector_3_out, bitselector_2_out);
  and and_4 (and_4_out, ~bitselector_3_out, and_2_out);  // AND_Gate
  Comparator #(.width(3)) comparator_3 (.a(in_1), .b(3'b011), .eq(comparator_3_eq));  // open: gt, lt
  BitSelector #(.width(2)) bitselector_4 (.in(bit_extender_1_out), .out(bitselector_4_out), .sel(1'b0));
  and and_5 (and_5_out, xor_2_out, xnor_1_out);
  and and_6 (and_6_out, xnor_1_out, Zero, comparator_3_eq, and_3_out);
  and and_7 (and_7_out, bitselector_4_out, and_5_out);
  or or_2 (Overflow, and_7_out, and_4_out, and_6_out);

  // Notes on the sheet:
  //   Result
endmodule

module Control_Unit (
  input  [4:0] in_1,
  output out_2,
  output out_3,
  output out_4,
  output out_5,
  output out_6,
  output out_7,
  output out_8
);

  wire demultiplexer_1_out1, demultiplexer_1_out2, demultiplexer_1_out3, demultiplexer_1_out4,
       demultiplexer_1_out5, demultiplexer_1_out6, demultiplexer_1_out7, demultiplexer_1_out8,
       demultiplexer_1_out20;

  Demultiplexer #(.select(5), .enable("false")) demultiplexer_1 (
    .out1(demultiplexer_1_out1), .out2(demultiplexer_1_out2), .out3(demultiplexer_1_out3),
    .out4(demultiplexer_1_out4), .out5(demultiplexer_1_out5), .out6(demultiplexer_1_out6),
    .out7(demultiplexer_1_out7), .out8(demultiplexer_1_out8), .out9(out_7), .out18(out_3), .out19(out_2),
    .out20(demultiplexer_1_out20), .out21(out_5), .out22(out_8), .in(1'b1), .sel(in_1));  // open: out0, out10, out11, out12, out13, out14, out15, out16, out17, out23, out24, out25, out26, out27, out28, out29, out30, out31
  nor nor_1 (out_4, demultiplexer_1_out1, demultiplexer_1_out2, demultiplexer_1_out3, demultiplexer_1_out4, demultiplexer_1_out5, demultiplexer_1_out6, demultiplexer_1_out7, demultiplexer_1_out8, out_7);
  or or_1 (out_6, demultiplexer_1_out20, out_5);
endmodule

module ALU_Control_Unit (
  input  [4:0] in_1,
  output [2:0] out_2
);

  wire demultiplexer_1_out1, demultiplexer_1_out2, demultiplexer_1_out3, demultiplexer_1_out6,
       demultiplexer_1_out7, demultiplexer_1_out8, demultiplexer_1_out10, demultiplexer_1_out11,
       demultiplexer_1_out12, demultiplexer_1_out15, demultiplexer_1_out16, demultiplexer_1_out17,
       demultiplexer_1_out18, demultiplexer_1_out19, or_1_out, or_2_out, or_3_out, or_4_out, or_5_out,
       or_6_out, or_7_out;

  Demultiplexer #(.select(5), .enable("false")) demultiplexer_1 (
    .out1(demultiplexer_1_out1), .out2(demultiplexer_1_out2), .out3(demultiplexer_1_out3),
    .out6(demultiplexer_1_out6), .out7(demultiplexer_1_out7), .out8(demultiplexer_1_out8),
    .out10(demultiplexer_1_out10), .out11(demultiplexer_1_out11), .out12(demultiplexer_1_out12),
    .out15(demultiplexer_1_out15), .out16(demultiplexer_1_out16), .out17(demultiplexer_1_out17),
    .out18(demultiplexer_1_out18), .out19(demultiplexer_1_out19), .in(1'b1), .sel(in_1));  // open: out0, out4, out5, out9, out13, out14, out20, out21, out22, out23, out24, out25, out26, out27, out28, out29, out30, out31
  or or_1 (or_1_out, demultiplexer_1_out18, demultiplexer_1_out19);
  or or_2 (or_2_out, demultiplexer_1_out1, or_1_out, demultiplexer_1_out10);
  or or_3 (or_3_out, demultiplexer_1_out2, demultiplexer_1_out11);
  or or_4 (or_4_out, demultiplexer_1_out3, demultiplexer_1_out12);
  or or_5 (or_5_out, demultiplexer_1_out6, demultiplexer_1_out15);
  or or_6 (or_6_out, demultiplexer_1_out7, demultiplexer_1_out16);
  or or_7 (or_7_out, demultiplexer_1_out8, demultiplexer_1_out17);
  Priority_Encoder priority_encoder_1 (
    .in1(or_2_out), .in2(or_3_out), .in3(or_4_out), .in4(or_5_out), .in5(or_6_out), .in6(or_7_out),
    .out(out_2));  // open: in0, in7, en_in, gs, en_out
endmodule

module test (
  input  [3:0] in_1,
  input  [7:0] in_2,
  input  in_3,
  input  in_4
);

  wire clock_1_out;
  wire [3:0] register_1_q;
  wire [7:0] register_2_q;

  Clock clock_1 (.out(clock_1_out));
  Register #(.width(4)) register_1 (.D(in_1), .Q(register_1_q), .clk(clock_1_out), .clr(in_4));  // open: en
  Register register_2 (.D(in_2), .Q(register_2_q), .clk(clock_1_out), .clr(in_4));  // open: en
  RAM #(.addrWidth(4), .bus("separate")) ram_1 (
    .addr(register_1_q), .din(register_2_q), .str(in_3), .clk(clock_1_out));  // open: data, sel, ld, clr
endmodule
